// Logisim project P1_Logic4.circ as structural Verilog: 1 circuit, main circuit P1_Logic4
module P1_Logic4 (
  input  a,
  input  b,
  input  c,
  input  d,
  output out1,
  output out2
);

  and and_1 (out1, a, b, c, d);
  or or_1 (out2, a, b, c, d);

  // Notes on the sheet:
  //   1. Four-input AND / OR
  //   INPUTS: a,b,c,d (1 bit each)                         OUTPUTS: out1, out2
  //   Check: 0000 -> out1=0, out2=0;   1111 -> out1=1, out2=1.
  //   AND: all four inputs = 1
  //   OR: at least one input = 1
endmodule
