// Logisim project P2_Mux8.circ as structural Verilog
module main (
  input  [7:0] din,
  input  [2:0] sel,
  output data
);

  p2_mux8_1 p2_mux8_1_1 (.din(din), .sel(sel), .data(data));

  // Notes on the sheet:
  //   din: initial=0xa5
  //   2. 8-to-1 Multiplexer
  //   sel = 000..111 selects din(0)..din(7).
endmodule

// VHDL entity p2_mux8_1, as the project stores it:
-- VHDL_1 homework; adapted from the course examples:
-- https://github.com/lizhuoh9/VHDL_code
-- Active-high display bus: display(7 downto 0) = a b c d e f g dp.
library ieee;
use ieee.std_logic_1164.all;
use ieee.numeric_std.all;

entity p2_mux8_1 is
    port (din : in std_logic_vector(7 downto 0);
          sel : in std_logic_vector(2 downto 0);
          data : out std_logic);
end p2_mux8_1;
architecture bhv of p2_mux8_1 is
begin
    process(din, sel)
    begin
        case sel is
            when "000" => data <= din(0);
            when "001" => data <= din(1);
            when "010" => data <= din(2);
            when "011" => data <= din(3);
            when "100" => data <= din(4);
            when "101" => data <= din(5);
            when "110" => data <= din(6);
            when "111" => data <= din(7);
            when others => data <= '0';
        end case;
    end process;
end architecture;
