// Logisim project P3_Letters.circ as structural Verilog: 1 circuit, main circuit P3_Letters
module P3_Letters (
  input  [2:0] code,
  output [7:0] display
);

  ROM #(.addrWidth(3), .dataWidth(8)) Letter_decoder (.addr(code), .data(display));
  _7_Segment_Display u_7_segment_display_1 (
    .g(display[1]), .f(display[2]), .a(display[7]), .b(display[6]), .e(display[3]), .d(display[4]),
    .c(display[5]), .dp(display[0]));

  // Other names for the same wires on the sheet: dp = display[0]; SEG[7:0] = display; g = display[1]; f = display[2];
  //   e = display[3]; d = display[4]; c = display[5]; b = display[6]; a = display[7]

  // Notes on the sheet:
  //   3. Letters on a 7-segment display
  //   INPUT: code[2:0]                                     OUTPUT: display[7:0] = abcdefgdp
  //   code: 0=A(a), 1=b, 2=C(c), 3=d, 4=F(f), 5=g; codes 6 and 7 = OFF.
  //   1 means segment ON. Decimal point is OFF. A,b,C,d,F,g are 7-segment glyphs.
  //   contents of Letter_decoder (hex, n*v repeats v):
  //   ee 3e 9c 7a 8e f6 00 00
endmodule
