// Logisim project P4_Vote25.circ as structural Verilog: 1 circuit, main circuit P4_Vote25
module P4_Vote25 (
  input  [24:0] vt,
  output result,
  output [4:0] count
);

  BitAdder #(.width(25)) bitadder_1 (.in0(vt), .out(count));
  Comparator #(.width(5), .mode("unsigned")) comparator_1 (.a(count), .b(5'b01100), .gt(result));  // open: eq, lt
  LED led_1 (.in(result));

  // Notes on the sheet:
  //   vt: initial=0x1fff
  //   4. 25-person voting machine
  //   INPUT: vt[24:0]                        OUTPUTS: count[4:0], result (pass/fail)
  //   result = 1 when count > 12, i.e. at least 13 of 25 votes are 1.
  //   Boundary checks: 12 ones -> 0; 13 ones -> 1; all zeros -> 0; all ones -> 1.
  //   Count ones
  //   Threshold = 12
  //   1 = passed; 0 = rejected
endmodule
