// Logisim project P5_Count13_Display.circ as structural Verilog: 1 circuit, main circuit P5_Count13_Display
module P5_Count13_Display (
  input  [12:0] vt,
  input  en,
  output [7:0] display,
  output [3:0] count
);

  wire [7:0] Hex_decoder_0__F_data;

  BitAdder #(.width(13)) bitadder_1 (.in0(vt), .out(count));
  ROM #(.addrWidth(4), .dataWidth(8)) Hex_decoder_0__F (.addr(count), .data(Hex_decoder_0__F_data));
  Multiplexer #(.select(1), .width(8), .enable("false")) multiplexer_1 (
    .in0({8{1'b0}}), .in1(Hex_decoder_0__F_data), .out(display), .sel(en));
  _7_Segment_Display u_7_segment_display_1 (
    .g(display[1]), .f(display[2]), .a(display[7]), .b(display[6]), .e(display[3]), .d(display[4]),
    .c(display[5]), .dp(display[0]));

  // Other names for the same wires on the sheet: N[3:0] = count; dp = display[0]; SEG[7:0] = display; g = display[1];
  //   f = display[2]; e = display[3]; d = display[4]; c = display[5]; b = display[6]; a = display[7]

  // Notes on the sheet:
  //   vt: initial=0x3ff
  //   en: initial=0x1
  //   5. Count 13 bits and display the total
  //   INPUTS: vt[12:0], en                         OUTPUTS: count[3:0], display[7:0]
  //   en=0: all segments OFF.  en=1: show 0..9, A, b, C or d (0..13).
  //   13 input bits cannot produce E(14) or F(15). The helper circuit tests the full decoder.
  //   Count ones
  //   contents of Hex_decoder_0__F (hex, n*v repeats v):
  //   fc 60 da f2 66 b6 be e0 fe f6 ee 3e 9c 7a 9e 8e
endmodule
