// Logisim project VHDL_Final.circ as structural Verilog: 6 circuits, main circuit P1_Logic4
module P1_Logic4 (
  input  a,
  input  b,
  input  c,
  input  d,
  output out1,
  output out2
);

  and and_1 (out1, a, b, c, d);
  or or_1 (out2, a, b, c, d);

  // Notes on the sheet:
  //   1. Four-input AND / OR
  //   INPUTS: a,b,c,d (1 bit each)                         OUTPUTS: out1, out2
  //   Check: 0000 -> out1=0, out2=0;   1111 -> out1=1, out2=1.
  //   AND: all four inputs = 1
  //   OR: at least one input = 1
endmodule

module P2_Mux8 (
  input  [7:0] din,
  input  [2:0] sel,
  output data
);

  Multiplexer #(.select(3), .width(1), .enable("false")) multiplexer_1 (
    .in0(din[0]), .in1(din[1]), .in2(din[2]), .in3(din[3]), .in4(din[4]), .in5(din[5]), .in6(din[6]),
    .in7(din[7]), .out(data), .sel(sel));

  // Notes on the sheet:
  //   din: initial=0xa5
  //   2. 8-to-1 multiplexer
  //   INPUTS: din[7:0], sel[2:0]                            OUTPUT: data (1 bit)
  //   sel=000 selects din[0]; sel=111 selects din[7]. All 2,048 input combinations tested.
  //   din[0]
  //   din[1]
  //   din[2]
  //   din[3]
  //   din[4]
  //   din[5]
  //   din[6]
  //   din[7]
endmodule

module P3_Letters (
  input  [2:0] code,
  output [7:0] display
);

  ROM #(.addrWidth(3), .dataWidth(8)) Letter_decoder (.addr(code), .data(display));
  _7_Segment_Display u_7_segment_display_1 (
    .g(display[1]), .f(display[2]), .a(display[7]), .b(display[6]), .e(display[3]), .d(display[4]),
    .c(display[5]), .dp(display[0]));

  // Other names for the same wires on the sheet: dp = display[0]; SEG[7:0] = display; g = display[1]; f = display[2];
  //   e = display[3]; d = display[4]; c = display[5]; b = display[6]; a = display[7]

  // Notes on the sheet:
  //   3. Letters on a 7-segment display
  //   INPUT: code[2:0]                                     OUTPUT: display[7:0] = abcdefgdp
  //   code: 0=A(a), 1=b, 2=C(c), 3=d, 4=F(f), 5=g; codes 6 and 7 = OFF.
  //   1 means segment ON. Decimal point is OFF. A,b,C,d,F,g are 7-segment glyphs.
  //   contents of Letter_decoder (hex, n*v repeats v):
  //   ee 3e 9c 7a 8e f6 00 00
endmodule

module P4_Vote25 (
  input  [24:0] vt,
  output result,
  output [4:0] count
);

  BitAdder #(.width(25)) bitadder_1 (.in0(vt), .out(count));
  Comparator #(.width(5), .mode("unsigned")) comparator_1 (.a(count), .b(5'b01100), .gt(result));  // open: eq, lt
  LED led_1 (.in(result));

  // Notes on the sheet:
  //   vt: initial=0x1fff
  //   4. 25-person voting machine
  //   INPUT: vt[24:0]                        OUTPUTS: count[4:0], result (pass/fail)
  //   result = 1 when count > 12, i.e. at least 13 of 25 votes are 1.
  //   Boundary checks: 12 ones -> 0; 13 ones -> 1; all zeros -> 0; all ones -> 1.
  //   Count ones
  //   Threshold = 12
  //   1 = passed; 0 = rejected
endmodule

module P5_Count13_Display (
  input  [12:0] vt,
  input  en,
  output [7:0] display,
  output [3:0] count
);

  wire [7:0] Hex_decoder_0__F_data;

  BitAdder #(.width(13)) bitadder_1 (.in0(vt), .out(count));
  ROM #(.addrWidth(4), .dataWidth(8)) Hex_decoder_0__F (.addr(count), .data(Hex_decoder_0__F_data));
  Multiplexer #(.select(1), .width(8), .enable("false")) multiplexer_1 (
    .in0({8{1'b0}}), .in1(Hex_decoder_0__F_data), .out(display), .sel(en));
  _7_Segment_Display u_7_segment_display_1 (
    .g(display[1]), .f(display[2]), .a(display[7]), .b(display[6]), .e(display[3]), .d(display[4]),
    .c(display[5]), .dp(display[0]));

  // Other names for the same wires on the sheet: N[3:0] = count; dp = display[0]; SEG[7:0] = display; g = display[1];
  //   f = display[2]; e = display[3]; d = display[4]; c = display[5]; b = display[6]; a = display[7]

  // Notes on the sheet:
  //   vt: initial=0x3ff
  //   en: initial=0x1
  //   5. Count 13 bits and display the total
  //   INPUTS: vt[12:0], en                         OUTPUTS: count[3:0], display[7:0]
  //   en=0: all segments OFF.  en=1: show 0..9, A, b, C or d (0..13).
  //   13 input bits cannot produce E(14) or F(15). The helper circuit tests the full decoder.
  //   Count ones
  //   contents of Hex_decoder_0__F (hex, n*v repeats v):
  //   fc 60 da f2 66 b6 be e0 fe f6 ee 3e 9c 7a 9e 8e
endmodule

module Hex_Decoder_Test (
  input  [3:0] dat,
  input  en,
  output [7:0] display
);

  wire [7:0] Hex_decoder_0__F_data;

  ROM #(.addrWidth(4), .dataWidth(8)) Hex_decoder_0__F (.addr(dat), .data(Hex_decoder_0__F_data));
  Multiplexer #(.select(1), .width(8), .enable("false")) multiplexer_1 (
    .in0({8{1'b0}}), .in1(Hex_decoder_0__F_data), .out(display), .sel(en));
  _7_Segment_Display u_7_segment_display_1 (
    .g(display[1]), .f(display[2]), .a(display[7]), .b(display[6]), .e(display[3]), .d(display[4]),
    .c(display[5]), .dp(display[0]));

  // Other names for the same wires on the sheet: N[3:0] = dat; dp = display[0]; SEG[7:0] = display; g = display[1];
  //   f = display[2]; e = display[3]; d = display[4]; c = display[5]; b = display[6]; a = display[7]

  // Notes on the sheet:
  //   en: initial=0x1
  //   Helper. Complete hexadecimal decoder
  //   INPUTS: dat[3:0], en                         OUTPUT: display[7:0]
  //   Decoder check: 0 1 2 3 4 5 6 7 8 9 A b C d E F; en=0 always turns it OFF.
  //   contents of Hex_decoder_0__F (hex, n*v repeats v):
  //   fc 60 da f2 66 b6 be e0 fe f6 ee 3e 9c 7a 9e 8e
endmodule
